// Logisim project mips-like.circ as structural Verilog: 12 circuits, main circuit PROCESSADOR
module PROCESSADOR (
  output [31:0] \INSTRUÇÃO 
);

  wire and_1_out, button_1_out, clock_1_out, ex_mem_1_out_11, ex_mem_1_out_12, ex_mem_1_out_13,
       ex_mem_1_out_14, ex_mem_1_out_15, id_ex_1_branch_2, id_ex_1_jump_2, id_ex_1_memread_2,
       id_ex_1_memto_reg, id_ex_1_memwrite_2, id_ex_1_ula_src_2, mem_wb_1_out_7, UC_branch, UC_jump,
       UC_memread, UC_memtoreg, UC_memwrite, UC_regdst, UC_regwrite, UC_ula_op0, UC_ula_op1, UC_ula_src,
       ula_1_branch, undriven;
  wire [1:0] id_ex_1_ula_op0_2;
  wire [3:0] ex_mem_1_out_18, id_ex_1_out_26, mem_wb_1_out_10, multiplexer_3_out, multiplexer_4_out;
  wire [19:0] ula_to_mem_1_saida;
  wire [31:0] adder_1_out, banco_de_registradores_1_r0_d, banco_de_registradores_1_r1_d, ex_mem_1_out_16,
       ex_mem_1_out_17, id_ex_1_out_23, id_ex_1_out_24, id_ex_1_out_25, if_id_1_out_5, mem_wb_1_out_8,
       mem_wb_1_out_9, multiplexer_1_out, multiplexer_2_out, multiplexer_5_out, multiplexer_6_out, PC_q,
       ram_1_data, rep_20_32_1_saida_32bits, rep_20_32_2_saida_32bits, rep_28_32_1_saida_32bits, rom_1_data,
       ula_1_ula_out;

  Multiplexer #(.width(32), .enable("false")) multiplexer_1 (
    .in0(if_id_1_out_5), .in1(rep_28_32_1_saida_32bits), .out(multiplexer_1_out), .sel(ex_mem_1_out_11));
  Multiplexer #(.width(32), .enable("false")) multiplexer_2 (
    .in0(multiplexer_1_out), .in1(rep_20_32_1_saida_32bits), .out(multiplexer_2_out), .sel(and_1_out));
  Register #(.width(32)) PC (.D(multiplexer_2_out), .Q(PC_q), .clk(clock_1_out), .clr(button_1_out));  // open: en
  Clock clock_1 (.out(clock_1_out));
  Adder #(.width(32)) adder_1 (.a(32'h4), .b(PC_q), .out(adder_1_out));  // open: cin, cout
  Button button_1 (.out(button_1_out));
  IF___ID if_id_1 (
    .add_4(adder_1_out), .pc(rom_1_data), .CLK(clock_1_out), .Clear(button_1_out), .out_5(if_id_1_out_5),
    .out_6(\INSTRUÇÃO ));
  ROM #(.dataWidth(32)) rom_1 (.addr(PC_q[9:2]), .data(rom_1_data));  // open: sel
  Multiplexer #(.width(4), .enable("false")) multiplexer_3 (
    .in0(\INSTRUÇÃO [27:24]), .in1(\INSTRUÇÃO [23:20]), .out(multiplexer_3_out), .sel(UC_regdst));
  Multiplexer #(.width(4), .enable("false")) multiplexer_4 (
    .in0(\INSTRUÇÃO [23:20]), .in1(\INSTRUÇÃO [19:16]), .out(multiplexer_4_out), .sel(UC_regdst));
  rep_28_32 rep_28_32_1 (.entra_28bits(\INSTRUÇÃO [27:0]), .saida_32bits(rep_28_32_1_saida_32bits));
  rep_20_32 rep_20_32_1 (.entrada_20bits(\INSTRUÇÃO [19:0]), .saida_32bits(rep_20_32_1_saida_32bits));
  UC UC (
    .E3(\INSTRUÇÃO [31]), .E2(\INSTRUÇÃO [30]), .E1(\INSTRUÇÃO [29]), .E0(\INSTRUÇÃO [28]),
    .RegDst(UC_regdst), .jump(UC_jump), .branch(UC_branch), .MemRead(UC_memread), .MemToReg(UC_memtoreg),
    .ula_op0(UC_ula_op0), .ula_op1(UC_ula_op1), .MemWrite(UC_memwrite), .ula_src(UC_ula_src),
    .RegWrite(UC_regwrite));
  BANCO_DE_REGISTRADORES banco_de_registradores_1 (
    .DATA_WRITE(multiplexer_6_out), .CLK(clock_1_out), .RW(mem_wb_1_out_10),
    .R0_D(banco_de_registradores_1_r0_d), .R0(multiplexer_3_out), .R1_D(banco_de_registradores_1_r1_d),
    .R1(multiplexer_4_out), .RW_2(UC_regwrite), .RESET(button_1_out));
  rep_20_32 rep_20_32_2 (.entrada_20bits(\INSTRUÇÃO [19:0]), .saida_32bits(rep_20_32_2_saida_32bits));
  ID___EX id_ex_1 (
    .jump(UC_jump), .branch(UC_branch), .MemRead(UC_memread), .MeToReg(UC_memtoreg), .ula_op0(UC_ula_op0),
    .ula_op1(UC_ula_op1), .MemWrite(UC_memwrite), .ula_src(UC_ula_src), .reg0(banco_de_registradores_1_r0_d),
    .data_write(rep_20_32_2_saida_32bits), .in_12(\INSTRUÇÃO [27:24]), .CLK(button_1_out),
    .Clear(clock_1_out), .jump_2(id_ex_1_jump_2), .branch_2(id_ex_1_branch_2), .MemRead_2(id_ex_1_memread_2),
    .MemTo_Reg(id_ex_1_memto_reg), .ula_op0_2(id_ex_1_ula_op0_2[0]), .ula_op1_2(id_ex_1_ula_op0_2[1]),
    .MemWrite_2(id_ex_1_memwrite_2), .ula_src_2(id_ex_1_ula_src_2), .out_23(id_ex_1_out_23),
    .out_24(id_ex_1_out_24), .out_25(id_ex_1_out_25), .out_26(id_ex_1_out_26),
    .reg1(banco_de_registradores_1_r1_d));
  ULA ula_1 (
    .DATA_0(id_ex_1_out_23), .DATA_1(multiplexer_5_out), .ULA_OUT(ula_1_ula_out), .ULA_OP(id_ex_1_ula_op0_2),
    .branch(ula_1_branch));
  Multiplexer #(.width(32), .enable("false")) multiplexer_5 (
    .in0(id_ex_1_out_24), .in1(id_ex_1_out_25), .out(multiplexer_5_out), .sel(id_ex_1_ula_src_2));
  EX___MEM ex_mem_1 (
    .in_1(id_ex_1_jump_2), .in_2(id_ex_1_branch_2), .in_3(ula_1_branch), .in_4(id_ex_1_memread_2),
    .in_5(id_ex_1_memwrite_2), .in_6(id_ex_1_out_24), .in_7(ula_1_ula_out), .in_8(id_ex_1_out_26),
    .CLK(clock_1_out), .CLEAR(button_1_out), .out_11(ex_mem_1_out_11), .out_12(ex_mem_1_out_12),
    .out_13(ex_mem_1_out_13), .out_14(ex_mem_1_out_14), .out_15(ex_mem_1_out_15), .out_16(ex_mem_1_out_16),
    .out_17(ex_mem_1_out_17), .out_18(ex_mem_1_out_18));
  ula_to_mem ula_to_mem_1 (.entrada(ex_mem_1_out_17), .saida(ula_to_mem_1_saida));
  and and_1 (and_1_out, ex_mem_1_out_12, ex_mem_1_out_13);
  RAM #(.addrWidth(20), .dataWidth(32), .bus("separate")) ram_1 (
    .addr(ula_to_mem_1_saida), .din(ex_mem_1_out_16), .data(ram_1_data), .str(ex_mem_1_out_15),
    .clk(clock_1_out), .ld(ex_mem_1_out_14), .clr(button_1_out));  // open: sel
  MEM___WB mem_wb_1 (
    .in_1(undriven), .in_2(ram_1_data), .in_3(ex_mem_1_out_17), ._24_27(ex_mem_1_out_18), .CLK(clock_1_out),
    .CLEAR(button_1_out), .out_7(mem_wb_1_out_7), .out_8(mem_wb_1_out_8), .out_9(mem_wb_1_out_9),
    .out_10(mem_wb_1_out_10));
  Multiplexer #(.width(32), .enable("false")) multiplexer_6 (
    .in0(mem_wb_1_out_9), .in1(mem_wb_1_out_8), .out(multiplexer_6_out), .sel(mem_wb_1_out_7));

  // Notes on the sheet:
  //   contents of rom_1 (hex, n*v repeats v):
  //   0 10000000 22000002 31000002 54200002 42400002 60200000 33*0 1000
  //   REG_1
  //   REG_0
  //   REG_W
  //   DATA_W
  //   BANCO DE REGISTRADORES
  //   REG0_D
  //   REG1_D
  //   ULA
endmodule

module ULA (
  input  [31:0] DATA_0,
  input  [31:0] DATA_1,
  input  [1:0] ULA_OP,
  output branch,
  output [31:0] ULA_OUT
);

  wire comparator_1_eq, comparator_1_gt;
  wire [31:0] adder_1_out, multiplier_1_out, shifter_1_out;

  Adder #(.width(32)) adder_1 (.a(DATA_0), .b(DATA_1), .out(adder_1_out));  // open: cin, cout
  Multiplier #(.width(32)) multiplier_1 (.a(DATA_0), .b(DATA_1), .out(multiplier_1_out));  // open: cin, cout
  Comparator #(.width(32), .mode("unsigned")) comparator_1 (
    .a(DATA_0), .b(DATA_1), .gt(comparator_1_gt), .eq(comparator_1_eq));  // open: lt
  Shifter #(.width(32)) shifter_1 (.in(DATA_0), .\dist (DATA_1[4:0]), .out(shifter_1_out));
  or or_1 (branch, comparator_1_gt, comparator_1_eq);
  Multiplexer #(.select(2), .width(32), .enable("false")) multiplexer_1 (
    .in0(adder_1_out), .in1(multiplier_1_out), .in2(DATA_1), .in3(shifter_1_out), .out(ULA_OUT), .sel(ULA_OP));
endmodule

module UC (
  input  E3,
  input  E2,
  input  E1,
  input  E0,
  output RegDst,
  output jump,
  output branch,
  output MemRead,
  output MemToReg,
  output ula_op0,
  output ula_op1,
  output MemWrite,
  output ula_src,
  output RegWrite
);

  wire and_1_out, and_2_out, and_3_out, and_4_out, and_5_out, and_6_out, and_7_out, and_8_out, and_9_out,
       and_10_out, and_11_out, and_12_out, and_13_out, and_14_out, and_15_out, and_16_out, and_17_out,
       and_18_out, and_19_out, and_20_out, and_21_out, and_22_out, and_23_out, and_24_out, and_25_out,
       and_26_out, and_27_out, not_1_out, not_2_out, not_3_out, not_4_out, not_5_out, not_6_out, not_7_out,
       not_8_out, not_9_out, not_10_out, not_11_out, not_12_out, not_13_out, not_14_out, not_15_out,
       not_16_out, not_17_out, not_18_out, not_19_out, not_20_out, not_21_out, not_22_out, not_23_out,
       not_24_out, not_25_out, not_26_out, not_27_out, not_28_out, not_29_out, not_30_out, not_31_out,
       not_32_out, not_33_out, not_34_out, not_35_out, not_36_out, not_37_out, not_38_out, not_39_out,
       not_40_out;

  not not_1 (not_1_out, E3);
  and and_1 (and_1_out, not_1_out, not_2_out);
  not not_2 (not_2_out, E2);
  not not_3 (not_3_out, E3);
  and and_2 (and_2_out, not_3_out, not_4_out, not_5_out);
  not not_4 (not_4_out, E1);
  not not_5 (not_5_out, E0);
  not not_6 (not_6_out, E2);
  and and_3 (and_3_out, E3, not_6_out, E0);
  and and_4 (and_4_out, E3, not_7_out, E1);
  not not_7 (not_7_out, E2);
  and and_5 (and_5_out, E3, E2, not_8_out);
  not not_8 (not_8_out, E1);
  and and_6 (and_6_out, E3, E2, not_9_out);
  not not_9 (not_9_out, E0);
  and and_7 (and_7_out, E3, not_10_out);
  not not_10 (not_10_out, E0);
  and and_8 (and_8_out, E3, E2, not_11_out);
  not not_11 (not_11_out, E1);
  and and_9 (and_9_out, E2, not_12_out, not_13_out);
  not not_12 (not_12_out, E1);
  not not_13 (not_13_out, E0);
  and and_10 (and_10_out, E3, E2, not_14_out);
  not not_14 (not_14_out, E0);
  not not_15 (not_15_out, E1);
  and and_11 (and_11_out, E2, not_15_out, not_16_out);
  not not_16 (not_16_out, E0);
  and and_12 (and_12_out, E3, E2, not_17_out);
  not not_17 (not_17_out, E0);
  not not_18 (not_18_out, E3);
  not not_19 (not_19_out, E2);
  not not_20 (not_20_out, E1);
  not not_21 (not_21_out, E2);
  not not_22 (not_22_out, E0);
  not not_23 (not_23_out, E0);
  and and_13 (and_13_out, E1, not_24_out);
  not not_24 (not_24_out, E0);
  and and_14 (and_14_out, E3, E2, not_25_out);
  not not_25 (not_25_out, E0);
  not not_26 (not_26_out, E3);
  not not_27 (not_27_out, E2);
  not not_28 (not_28_out, E0);
  not not_29 (not_29_out, E3);
  not not_30 (not_30_out, E2);
  and and_15 (and_15_out, not_29_out, not_30_out, E1);
  not not_31 (not_31_out, E2);
  and and_16 (and_16_out, not_31_out, E1, E0);
  and and_17 (and_17_out, E2, not_32_out);
  not not_32 (not_32_out, E1);
  not not_33 (not_33_out, E3);
  and and_18 (and_18_out, not_33_out, E2, E0);
  and and_19 (and_19_out, E3, E2, not_34_out);
  not not_34 (not_34_out, E0);
  not not_35 (not_35_out, E3);
  and and_20 (and_20_out, not_35_out, not_36_out);
  not not_36 (not_36_out, E2);
  not not_37 (not_37_out, E3);
  and and_21 (and_21_out, not_37_out, not_38_out);
  not not_38 (not_38_out, E1);
  not not_39 (not_39_out, E3);
  and and_22 (and_22_out, not_39_out, not_40_out);
  not not_40 (not_40_out, E0);
  or or_1 (RegDst, and_1_out, and_2_out);
  or or_2 (jump, and_3_out, and_4_out, and_5_out, and_6_out);
  or or_3 (branch, and_7_out, and_8_out);
  or or_4 (MemRead, and_9_out, and_10_out);
  or or_5 (MemToReg, and_11_out, and_12_out);
  and and_23 (and_23_out, not_18_out, not_19_out, not_20_out, E0);
  or or_6 (ula_op0, and_23_out, and_24_out, and_25_out);
  and and_24 (and_24_out, not_21_out, E1, not_22_out);
  and and_25 (and_25_out, E3, E2, not_23_out);
  or or_7 (ula_op1, and_13_out, and_14_out);
  and and_26 (and_26_out, not_26_out, E2, E0);
  or or_8 (MemWrite, and_26_out, and_27_out);
  and and_27 (and_27_out, E3, not_27_out, E1, not_28_out);
  or or_9 (ula_src, and_15_out, and_16_out, and_17_out, and_18_out, and_19_out);
  or or_10 (RegWrite, and_20_out, and_21_out, and_22_out);
endmodule

module BANCO_DE_REGISTRADORES (
  input  [31:0] DATA_WRITE,
  input  [3:0] R0,
  input  [3:0] R1,
  input  CLK,
  input  [3:0] RW,
  input  RESET,
  input  RW_2,
  output [31:0] R0_D,
  output [31:0] R1_D
);

  wire demultiplexer_1_out0, demultiplexer_1_out1, demultiplexer_1_out2, demultiplexer_1_out3,
       demultiplexer_1_out4, demultiplexer_1_out5, demultiplexer_1_out6, demultiplexer_1_out7,
       demultiplexer_1_out8, demultiplexer_1_out9, demultiplexer_1_out10, demultiplexer_1_out11,
       demultiplexer_1_out12, demultiplexer_1_out13, demultiplexer_1_out14, demultiplexer_1_out15;
  wire [31:0] register_1_q, register_2_q, register_3_q, register_4_q, register_5_q, register_6_q,
       register_7_q, register_8_q, register_9_q, register_10_q, register_11_q, register_12_q, register_13_q,
       register_14_q, register_15_q, register_16_q;

  Demultiplexer #(.select(4), .enable("false")) demultiplexer_1 (
    .out0(demultiplexer_1_out0), .out1(demultiplexer_1_out1), .out2(demultiplexer_1_out2),
    .out3(demultiplexer_1_out3), .out4(demultiplexer_1_out4), .out5(demultiplexer_1_out5),
    .out6(demultiplexer_1_out6), .out7(demultiplexer_1_out7), .out8(demultiplexer_1_out8),
    .out9(demultiplexer_1_out9), .out10(demultiplexer_1_out10), .out11(demultiplexer_1_out11),
    .out12(demultiplexer_1_out12), .out13(demultiplexer_1_out13), .out14(demultiplexer_1_out14),
    .out15(demultiplexer_1_out15), .in(RW_2), .sel(RW));
  Register #(.width(32)) register_1 (
    .D(DATA_WRITE), .en(demultiplexer_1_out0), .Q(register_1_q), .clk(CLK), .clr(RESET));
  Register #(.width(32)) register_2 (
    .D(DATA_WRITE), .en(demultiplexer_1_out1), .Q(register_2_q), .clk(CLK), .clr(RESET));
  Register #(.width(32)) register_3 (
    .D(DATA_WRITE), .en(demultiplexer_1_out2), .Q(register_3_q), .clk(CLK), .clr(RESET));
  Register #(.width(32)) register_4 (
    .D(DATA_WRITE), .en(demultiplexer_1_out3), .Q(register_4_q), .clk(CLK), .clr(RESET));
  Register #(.width(32)) register_5 (
    .D(DATA_WRITE), .en(demultiplexer_1_out4), .Q(register_5_q), .clk(CLK), .clr(RESET));
  Register #(.width(32)) register_6 (
    .D(DATA_WRITE), .en(demultiplexer_1_out5), .Q(register_6_q), .clk(CLK), .clr(RESET));
  Register #(.width(32)) register_7 (
    .D(DATA_WRITE), .en(demultiplexer_1_out6), .Q(register_7_q), .clk(CLK), .clr(RESET));
  Register #(.width(32)) register_8 (
    .D(DATA_WRITE), .en(demultiplexer_1_out7), .Q(register_8_q), .clk(CLK), .clr(RESET));
  Register #(.width(32)) register_9 (
    .D(DATA_WRITE), .en(demultiplexer_1_out8), .Q(register_9_q), .clk(CLK), .clr(RESET));
  Register #(.width(32)) register_10 (
    .D(DATA_WRITE), .en(demultiplexer_1_out9), .Q(register_10_q), .clk(CLK), .clr(RESET));
  Register #(.width(32)) register_11 (
    .D(DATA_WRITE), .en(demultiplexer_1_out10), .Q(register_11_q), .clk(CLK), .clr(RESET));
  Register #(.width(32)) register_12 (
    .D(DATA_WRITE), .en(demultiplexer_1_out11), .Q(register_12_q), .clk(CLK), .clr(RESET));
  Register #(.width(32)) register_13 (
    .D(DATA_WRITE), .en(demultiplexer_1_out12), .Q(register_13_q), .clk(CLK), .clr(RESET));
  Register #(.width(32)) register_14 (
    .D(DATA_WRITE), .en(demultiplexer_1_out13), .Q(register_14_q), .clk(CLK), .clr(RESET));
  Register #(.width(32)) register_15 (
    .D(DATA_WRITE), .en(demultiplexer_1_out14), .Q(register_15_q), .clk(CLK), .clr(RESET));
  Register #(.width(32)) register_16 (
    .D(DATA_WRITE), .en(demultiplexer_1_out15), .Q(register_16_q), .clk(CLK), .clr(RESET));
  Multiplexer #(.select(4), .width(32), .disabled(0), .enable("false")) multiplexer_1 (
    .in0(register_1_q), .in1(register_2_q), .in2(register_3_q), .in3(register_4_q), .in4(register_5_q),
    .in5(register_6_q), .in6(register_7_q), .in7(register_8_q), .in8(register_9_q), .in9(register_10_q),
    .in10(register_11_q), .in11(register_12_q), .in12(register_13_q), .in13(register_14_q),
    .in14(register_15_q), .in15(register_16_q), .out(R0_D), .sel(R0));
  Multiplexer #(.select(4), .width(32), .enable("false")) multiplexer_2 (
    .in0(register_1_q), .in1(register_2_q), .in2(register_3_q), .in3(register_4_q), .in4(register_5_q),
    .in5(register_6_q), .in6(register_7_q), .in7(register_8_q), .in8(register_9_q), .in9(register_10_q),
    .in10(register_11_q), .in11(register_12_q), .in12(register_13_q), .in13(register_14_q),
    .in14(register_15_q), .in15(register_16_q), .out(R1_D), .sel(R1));
endmodule

module rep_16_32 (
  input  [15:0] entrada,
  output [31:0] saida
);


  assign saida = {{16{1'b0}}, entrada};
endmodule

module rep_20_32 (
  input  [19:0] entrada_20bits,
  output [31:0] saida_32bits
);


  assign saida_32bits = {{12{1'b0}}, entrada_20bits};
endmodule

module rep_28_32 (
  input  [27:0] entra_28bits,
  output [31:0] saida_32bits
);


  assign saida_32bits = {4'b0000, entra_28bits};
endmodule

module ula_to_mem (
  input  [31:0] entrada,
  output [19:0] saida
);


  assign saida = entrada[19:0];
endmodule

module IF___ID (
  input  [31:0] add_4,
  input  [31:0] pc,
  input  CLK,
  input  Clear,
  output [31:0] out_5,
  output [31:0] out_6
);

  Register #(.width(32)) register_1 (.D(add_4), .en(1'b1), .Q(out_5), .clk(CLK), .clr(Clear));
  Register #(.width(32)) register_2 (.D(pc), .en(1'b1), .Q(out_6), .clk(CLK), .clr(Clear));
endmodule

module ID___EX (
  input  jump,
  input  branch,
  input  MemRead,
  input  MeToReg,
  input  ula_op0,
  input  ula_op1,
  input  MemWrite,
  input  ula_src,
  input  [31:0] reg0,
  input  [31:0] reg1,
  input  [31:0] data_write,
  input  [3:0] in_12,
  input  CLK,
  input  Clear,
  output jump_2,
  output branch_2,
  output MemRead_2,
  output MemTo_Reg,
  output ula_op0_2,
  output ula_op1_2,
  output MemWrite_2,
  output ula_src_2,
  output [31:0] out_23,
  output [31:0] out_24,
  output [31:0] out_25,
  output [3:0] out_26
);

  Register #(.width(1)) register_1 (.D(jump), .en(1'b1), .Q(jump_2), .clk(CLK), .clr(Clear));
  Register #(.width(1)) register_2 (.D(branch), .en(1'b1), .Q(branch_2), .clk(CLK), .clr(Clear));
  Register #(.width(1)) register_3 (.D(MemRead), .en(1'b1), .Q(MemRead_2), .clk(CLK), .clr(Clear));
  Register #(.width(1)) register_4 (.D(MeToReg), .en(1'b1), .Q(MemTo_Reg), .clk(CLK), .clr(Clear));
  Register #(.width(1)) register_5 (.D(ula_op0), .en(1'b1), .Q(ula_op0_2), .clk(CLK), .clr(Clear));
  Register #(.width(1)) register_6 (.D(ula_op1), .en(1'b1), .Q(ula_op1_2), .clk(CLK), .clr(Clear));
  Register #(.width(1)) register_7 (.D(MemWrite), .en(1'b1), .Q(MemWrite_2), .clk(CLK), .clr(Clear));
  Register #(.width(1)) register_8 (.D(ula_src), .en(1'b1), .Q(ula_src_2), .clk(CLK), .clr(Clear));
  Register #(.width(32)) register_9 (.D(reg0), .en(1'b1), .Q(out_23), .clk(CLK), .clr(Clear));
  Register #(.width(32)) register_10 (.D(reg1), .en(1'b1), .Q(out_24), .clk(CLK), .clr(Clear));
  Register #(.width(32)) register_11 (.D(data_write), .en(1'b1), .Q(out_25), .clk(CLK), .clr(Clear));
  Register #(.width(4)) register_12 (.D(in_12), .en(1'b1), .Q(out_26), .clk(CLK), .clr(Clear));
endmodule

module EX___MEM (
  input  in_1,
  input  in_2,
  input  in_3,
  input  in_4,
  input  in_5,
  input  [31:0] in_6,
  input  [31:0] in_7,
  input  [3:0] in_8,
  input  CLK,
  input  CLEAR,
  output out_11,
  output out_12,
  output out_13,
  output out_14,
  output out_15,
  output [31:0] out_16,
  output [31:0] out_17,
  output [3:0] out_18
);

  Register #(.width(1)) register_1 (.D(in_1), .en(1'b1), .Q(out_11), .clk(CLK), .clr(CLEAR));
  Register #(.width(1)) register_2 (.D(in_2), .en(1'b1), .Q(out_12), .clk(CLK), .clr(CLEAR));
  Register #(.width(1)) register_3 (.D(in_3), .en(1'b1), .Q(out_13), .clk(CLK), .clr(CLEAR));
  Register #(.width(1)) register_4 (.D(in_4), .en(1'b1), .Q(out_14), .clk(CLK), .clr(CLEAR));
  Register #(.width(1)) register_5 (.D(in_5), .en(1'b1), .Q(out_15), .clk(CLK), .clr(CLEAR));
  Register #(.width(32)) register_6 (.D(in_6), .en(1'b1), .Q(out_16), .clk(CLK), .clr(CLEAR));
  Register #(.width(32)) register_7 (.D(in_7), .en(1'b1), .Q(out_17), .clk(CLK), .clr(CLEAR));
  Register #(.width(4)) register_8 (.D(in_8), .en(1'b1), .Q(out_18), .clk(CLK), .clr(CLEAR));
endmodule

module MEM___WB (
  input  in_1,
  input  [31:0] in_2,
  input  [31:0] in_3,
  input  [3:0] _24_27,
  input  CLK,
  input  CLEAR,
  output out_7,
  output [31:0] out_8,
  output [31:0] out_9,
  output [3:0] out_10
);

  Register #(.width(1)) register_1 (.D(in_1), .en(1'b1), .Q(out_7), .clk(CLK), .clr(CLEAR));
  Register #(.width(32)) register_2 (.D(in_2), .en(1'b1), .Q(out_8), .clk(CLK), .clr(CLEAR));
  Register #(.width(32)) register_3 (.D(in_3), .en(1'b1), .Q(out_9), .clk(CLK), .clr(CLEAR));
  Register #(.width(4)) register_4 (.D(_24_27), .en(1'b1), .Q(out_10), .clk(CLK), .clr(CLEAR));
endmodule
